# Fritzing sketch button (saved by Fritzing 0.9.2b)
breadboards: 1

parts:
  S1 = Pushbutton [package="[SMD]"]
  TRINKET1 = Trinket 3V
  R1 = Resistor [tolerance=±5% resistance=330 package="2010 [SMD]"]
  LED1 = smd LED [color="Yellow (595nm)" package="1206 [SMD]"]
  LED2 = smd LED [color="Green (565nm)" package="1206 [SMD]"]

nets:
  N1: S1.Pin_1, S1.Pin_2
  N2: S1.Pin_3, S1.Pin_4, TRINKET1.no_name_yet#2, TRINKET1.no_name_yet#9, R1.Pin_0
  N3: TRINKET1.no_name_yet#7, LED2.anode
  N4: TRINKET1.no_name_yet#8, LED1.anode
  N5: R1.Pin_1, LED1.cathode, LED2.cathode

custom parts:
  Trinket 3V: Adafruit Trinket 3V
